// Logisim project risc_cpu_simulation.circ as structural Verilog: 22 circuits, main circuit main
module main (
  input  in_1
);

  wire clock_1_out, clock_2_out, decode_stage_1_branch_out, decode_stage_1_jump_out,
       decode_stage_1_mem_rd_out, decode_stage_1_mem_wr_out, decode_stage_1_s1_sel_out,
       decode_stage_1_s2_sel_out, decode_stage_1_wb_out, ex_mem_reg_1_mem_rd_out, ex_mem_reg_1_mem_wr_out,
       ex_mem_reg_1_wb_out, ex_stage_1_flush, ex_stage_1_mem_rd_out, ex_stage_1_mem_wr_out,
       ex_stage_1_pc_sel, ex_stage_1_wb_out, forwarding_unit_1_ex_rs1_sel, forwarding_unit_1_ex_rs2_sel,
       forwarding_unit_1_mem_rs_sel, forwarding_unit_1_stall, i_memory_1_stall, id_ex_reg_1_branch_out,
       id_ex_reg_1_jump_out, id_ex_reg_1_mem_rd_out, id_ex_reg_1_mem_wr_out, id_ex_reg_1_s1_sel_out,
       id_ex_reg_1_s2_sel_out, id_ex_reg_1_wb_out, mem_wb_reg_1_wb_out, memoryaccess_stage_1_rd,
       memoryaccess_stage_1_wb_out, memoryaccess_stage_1_wr, or_1_out, writeback_stage_1_wb_out;
  wire [1:0] decode_stage_1_wb_sel_out, ex_mem_reg_1_wb_sel_out, ex_stage_1_wb_sel_out,
       id_ex_reg_1_wb_sel_out, mem_wb_reg_1_wb_sel_out, memoryaccess_stage_1_wb_sel_out;
  wire [2:0] decode_stage_1_funct3_out, ex_mem_reg_1_funct3_out, ex_stage_1_funct3_out,
       id_ex_reg_1_funct3_out, memoryaccess_stage_1_funct3_out;
  wire [4:0] decode_stage_1_rd_sel_out, decode_stage_1_rs1_sel_out, decode_stage_1_rs2_sel_out,
       ex_mem_reg_1_rd_sel_out, ex_mem_reg_1_rs2_sel_out, ex_stage_1_rd_sel_out, ex_stage_1_rs2_sel_out,
       id_ex_reg_1_rd_sel_out, id_ex_reg_1_rs1_sel_out, id_ex_reg_1_rs2_sel_out, mem_wb_reg_1_rd_sel_out,
       memoryaccess_stage_1_rd_sel_out, writeback_stage_1_rd_sel_out;
  wire [6:0] decode_stage_1_funct7_out, id_ex_reg_1_funct7_out;
  wire [31:0] d_memory_1_data_out, decode_stage_1_imm_out, decode_stage_1_next_pc_out, decode_stage_1_pc_out,
       decode_stage_1_rs1_out, decode_stage_1_rs2_out, ex_mem_reg_1_imm_out, ex_mem_reg_1_next_pc_out,
       ex_mem_reg_1_pc_out, ex_mem_reg_1_result_out, ex_mem_reg_1_rs2_out, ex_stage_1_imm_out,
       ex_stage_1_next_pc_out, ex_stage_1_pc_out, ex_stage_1_result_out, ex_stage_1_rs2_out,
       fetch_stage_1_address, fetch_stage_1_instr_out, fetch_stage_1_next_pc, fetch_stage_1_pc_out,
       forwarding_unit_1_ex_rs1_data, forwarding_unit_1_ex_rs2_data, forwarding_unit_1_mem_rs_data,
       i_memory_1_instr, id_ex_reg_1_imm_out, id_ex_reg_1_next_pc_out, id_ex_reg_1_pc_out,
       id_ex_reg_1_rs1_out, id_ex_reg_1_rs2_out, if_id_reg_1_instr_out, if_id_reg_1_next_pc_out,
       if_id_reg_1_pc_out, mem_wb_reg_1_a_result_out, mem_wb_reg_1_imm_out, mem_wb_reg_1_m_result_out,
       mem_wb_reg_1_next_pc_out, mem_wb_reg_1_pc_out, memoryaccess_stage_1_a_result_out,
       memoryaccess_stage_1_addr, memoryaccess_stage_1_d_out, memoryaccess_stage_1_forward_d,
       memoryaccess_stage_1_imm_out, memoryaccess_stage_1_m_result_out, memoryaccess_stage_1_next_pc_out,
       memoryaccess_stage_1_pc_out, multiplexer_1_out, multiplexer_2_out, multiplexer_3_out,
       writeback_stage_1_result;

  Clock #(.highDuration(2), .lowDuration(2), .phaseOffset(1)) clock_1 (.out(clock_1_out));
  Clock #(.highDuration(2), .lowDuration(2)) clock_2 (.out(clock_2_out));
  Fetch_Stage fetch_stage_1 (
    .Branch_PC(ex_stage_1_result_out), .PC_Sel(ex_stage_1_pc_sel), .Stall(forwarding_unit_1_stall),
    .Clk(clock_1_out), .Reset(in_1), .Mem_Stall(i_memory_1_stall), .Instr_In(i_memory_1_instr),
    .PC_Out(fetch_stage_1_pc_out), .Next_PC(fetch_stage_1_next_pc), .Instr_Out(fetch_stage_1_instr_out),
    .Address(fetch_stage_1_address));
  I_Memory i_memory_1 (
    .Addr(fetch_stage_1_address), .Clk(clock_1_out), .Reset(in_1), .Instr(i_memory_1_instr),
    .Stall(i_memory_1_stall));
  IF_ID_Reg if_id_reg_1 (
    .PC_In(fetch_stage_1_pc_out), .Next_PC_In(fetch_stage_1_next_pc), .Instr_In(fetch_stage_1_instr_out),
    .Stall(forwarding_unit_1_stall), .Clk(clock_1_out), .Reset(or_1_out), .PC_Out(if_id_reg_1_pc_out),
    .Next_PC_Out(if_id_reg_1_next_pc_out), .Instr_Out(if_id_reg_1_instr_out));
  or or_1 (or_1_out, in_1, ex_stage_1_flush);
  Decode_Stage decode_stage_1 (
    .PC_In(if_id_reg_1_pc_out), .Next_PC_In(if_id_reg_1_next_pc_out), .Instr_In(if_id_reg_1_instr_out),
    .D(writeback_stage_1_result), .RD_Sel(writeback_stage_1_rd_sel_out), .WE(writeback_stage_1_wb_out),
    .Clk(clock_1_out), .Reset(in_1), .PC_Out(decode_stage_1_pc_out),
    .Next_PC_Out(decode_stage_1_next_pc_out), .Jump_Out(decode_stage_1_jump_out),
    .Branch_Out(decode_stage_1_branch_out), .S1_Sel_Out(decode_stage_1_s1_sel_out),
    .S2_Sel_Out(decode_stage_1_s2_sel_out), .Mem_RD_Out(decode_stage_1_mem_rd_out),
    .Mem_WR_Out(decode_stage_1_mem_wr_out), .WB_Out(decode_stage_1_wb_out),
    .WB_Sel_Out(decode_stage_1_wb_sel_out), .Funct3_Out(decode_stage_1_funct3_out),
    .Funct7_Out(decode_stage_1_funct7_out), .RS1_Sel_Out(decode_stage_1_rs1_sel_out),
    .RS2_Sel_Out(decode_stage_1_rs2_sel_out), .RD_Sel_Out(decode_stage_1_rd_sel_out),
    .RS1_Out(decode_stage_1_rs1_out), .RS2_Out(decode_stage_1_rs2_out), .Imm_Out(decode_stage_1_imm_out));
  ID_EX_Reg id_ex_reg_1 (
    .Stall(forwarding_unit_1_stall), .Clk(clock_1_out), .Reset(in_1), .Mem_WR_In(decode_stage_1_mem_wr_out),
    .WB_In(decode_stage_1_wb_out), .PC_In(decode_stage_1_pc_out), .WB_Sel_In(decode_stage_1_wb_sel_out),
    .Funct3_In(decode_stage_1_funct3_out), .Funct7_In(decode_stage_1_funct7_out),
    .RS1_Sel_In(decode_stage_1_rs1_sel_out), .RS2_Sel_In(decode_stage_1_rs2_sel_out),
    .RD_Sel_In(decode_stage_1_rd_sel_out), .RS1_In(decode_stage_1_rs1_out), .RS2_In(decode_stage_1_rs2_out),
    .Imm_In(decode_stage_1_imm_out), .Next_PC_In(decode_stage_1_next_pc_out),
    .Jump_In(decode_stage_1_jump_out), .Branch_In(decode_stage_1_branch_out),
    .S1_Sel_In(decode_stage_1_s1_sel_out), .S2_Sel_In(decode_stage_1_s2_sel_out),
    .Mem_RD_In(decode_stage_1_mem_rd_out), .Mem_WR_Out(id_ex_reg_1_mem_wr_out), .WB_Out(id_ex_reg_1_wb_out),
    .PC_Out(id_ex_reg_1_pc_out), .WB_Sel_Out(id_ex_reg_1_wb_sel_out), .Funct3_Out(id_ex_reg_1_funct3_out),
    .Funct7_Out(id_ex_reg_1_funct7_out), .RS1_Sel_Out(id_ex_reg_1_rs1_sel_out),
    .RS2_Sel_Out(id_ex_reg_1_rs2_sel_out), .RD_Sel_Out(id_ex_reg_1_rd_sel_out),
    .RS1_Out(id_ex_reg_1_rs1_out), .RS2_Out(id_ex_reg_1_rs2_out), .Imm_Out(id_ex_reg_1_imm_out),
    .Next_PC_Out(id_ex_reg_1_next_pc_out), .Jump_Out(id_ex_reg_1_jump_out),
    .Branch_Out(id_ex_reg_1_branch_out), .S1_Sel_Out(id_ex_reg_1_s1_sel_out),
    .S2_Sel_Out(id_ex_reg_1_s2_sel_out), .Mem_RD_Out(id_ex_reg_1_mem_rd_out));
  Multiplexer #(.width(32)) multiplexer_1 (
    .in0(id_ex_reg_1_rs1_out), .in1(forwarding_unit_1_ex_rs1_data), .out(multiplexer_1_out),
    .sel(forwarding_unit_1_ex_rs1_sel));
  Forwarding_Unit forwarding_unit_1 (
    .RD(ex_mem_reg_1_mem_rd_out), .Mem_WB(ex_mem_reg_1_wb_out), .Mem_Reg(ex_mem_reg_1_rd_sel_out),
    .Mem_Data(memoryaccess_stage_1_forward_d), .WB_WB(writeback_stage_1_wb_out),
    .WB_Reg(writeback_stage_1_rd_sel_out), .WB_Data(writeback_stage_1_result),
    .EX_RS1(id_ex_reg_1_rs1_sel_out), .EX_RS2(id_ex_reg_1_rs2_sel_out), .MEM_RS(ex_mem_reg_1_rs2_sel_out),
    .EX_RS1_Sel(forwarding_unit_1_ex_rs1_sel), .EX_RS1_Data(forwarding_unit_1_ex_rs1_data),
    .EX_RS2_Sel(forwarding_unit_1_ex_rs2_sel), .EX_RS2_Data(forwarding_unit_1_ex_rs2_data),
    .MEM_RS_Sel(forwarding_unit_1_mem_rs_sel), .MEM_RS_Data(forwarding_unit_1_mem_rs_data),
    .Stall(forwarding_unit_1_stall));
  Multiplexer #(.width(32)) multiplexer_2 (
    .in0(id_ex_reg_1_rs2_out), .in1(forwarding_unit_1_ex_rs2_data), .out(multiplexer_2_out),
    .sel(forwarding_unit_1_ex_rs2_sel));
  EX_Stage ex_stage_1 (
    .PC_In(id_ex_reg_1_pc_out), .Next_PC_In(id_ex_reg_1_next_pc_out), .Jump_In(id_ex_reg_1_jump_out),
    .Branch_In(id_ex_reg_1_branch_out), .S1_Sel_In(id_ex_reg_1_s1_sel_out),
    .S2_Sel_In(id_ex_reg_1_s2_sel_out), .Mem_RD_In(id_ex_reg_1_mem_rd_out),
    .Mem_WR_In(id_ex_reg_1_mem_wr_out), .WB_In(id_ex_reg_1_wb_out), .WB_Sel_In(id_ex_reg_1_wb_sel_out),
    .Funct3_In(id_ex_reg_1_funct3_out), .Funct7_In(id_ex_reg_1_funct7_out),
    .RS1_Sel_In(id_ex_reg_1_rs1_sel_out), .RS2_Sel_In(id_ex_reg_1_rs2_sel_out),
    .RD_Sel_In(id_ex_reg_1_rd_sel_out), .RS1_In(multiplexer_1_out), .RS2_In(multiplexer_2_out),
    .Imm_In(id_ex_reg_1_imm_out), .Clk(clock_1_out), .Clk90(clock_2_out), .PC_Out(ex_stage_1_pc_out),
    .Next_PC_Out(ex_stage_1_next_pc_out), .Mem_RD_Out(ex_stage_1_mem_rd_out),
    .Mem_WR_Out(ex_stage_1_mem_wr_out), .WB_Out(ex_stage_1_wb_out), .WB_Sel_Out(ex_stage_1_wb_sel_out),
    .Funct3_Out(ex_stage_1_funct3_out), .RS2_Sel_Out(ex_stage_1_rs2_sel_out),
    .RD_Sel_Out(ex_stage_1_rd_sel_out), .RS2_Out(ex_stage_1_rs2_out), .Result_Out(ex_stage_1_result_out),
    .Imm_Out(ex_stage_1_imm_out), .PC_Sel(ex_stage_1_pc_sel), .Flush(ex_stage_1_flush));
  EX_MEM_Reg ex_mem_reg_1 (
    .PC_In(ex_stage_1_pc_out), .RS2_Sel_In(ex_stage_1_rs2_sel_out), .RD_Sel_In(ex_stage_1_rd_sel_out),
    .RS2_In(ex_stage_1_rs2_out), .Result_In(ex_stage_1_result_out), .Imm_In(ex_stage_1_imm_out), .WE(1'b1),
    .Clk(clock_1_out), .Reset(in_1), .Next_PC_In(ex_stage_1_next_pc_out), .Mem_RD_In(ex_stage_1_mem_rd_out),
    .Mem_WR_In(ex_stage_1_mem_wr_out), .WB_In(ex_stage_1_wb_out), .WB_Sel_In(ex_stage_1_wb_sel_out),
    .Funct3_In(ex_stage_1_funct3_out), .PC_Out(ex_mem_reg_1_pc_out), .RS2_Sel_Out(ex_mem_reg_1_rs2_sel_out),
    .RD_Sel_Out(ex_mem_reg_1_rd_sel_out), .RS2_Out(ex_mem_reg_1_rs2_out),
    .Result_Out(ex_mem_reg_1_result_out), .Imm_Out(ex_mem_reg_1_imm_out),
    .Next_PC_Out(ex_mem_reg_1_next_pc_out), .Mem_RD_Out(ex_mem_reg_1_mem_rd_out),
    .Mem_WR_Out(ex_mem_reg_1_mem_wr_out), .WB_Out(ex_mem_reg_1_wb_out), .WB_Sel_Out(ex_mem_reg_1_wb_sel_out),
    .Funct3_Out(ex_mem_reg_1_funct3_out));
  Multiplexer #(.width(32)) multiplexer_3 (
    .in0(ex_mem_reg_1_rs2_out), .in1(forwarding_unit_1_mem_rs_data), .out(multiplexer_3_out),
    .sel(forwarding_unit_1_mem_rs_sel));
  MemoryAccess_Stage memoryaccess_stage_1 (
    .PC_In(ex_mem_reg_1_pc_out), .Next_PC_In(ex_mem_reg_1_next_pc_out), .Mem_RD_In(ex_mem_reg_1_mem_rd_out),
    .Mem_WR_In(ex_mem_reg_1_mem_wr_out), .WB_In(ex_mem_reg_1_wb_out), .WB_Sel_In(ex_mem_reg_1_wb_sel_out),
    .Funct3_In(ex_mem_reg_1_funct3_out), .RS2_Sel_In(ex_mem_reg_1_rs2_sel_out),
    .RD_Sel_In(ex_mem_reg_1_rd_sel_out), .RS2_In(multiplexer_3_out), .Result_In(ex_mem_reg_1_result_out),
    .Imm_In(ex_mem_reg_1_imm_out), .D_In(d_memory_1_data_out), .Mem_Stall(1'b0),
    .PC_Out(memoryaccess_stage_1_pc_out), .Next_PC_Out(memoryaccess_stage_1_next_pc_out),
    .WB_Out(memoryaccess_stage_1_wb_out), .WB_Sel_Out(memoryaccess_stage_1_wb_sel_out),
    .RD_Sel_Out(memoryaccess_stage_1_rd_sel_out), .A_Result_Out(memoryaccess_stage_1_a_result_out),
    .M_Result_Out(memoryaccess_stage_1_m_result_out), .Imm_Out(memoryaccess_stage_1_imm_out),
    .Forward_D(memoryaccess_stage_1_forward_d), .Addr(memoryaccess_stage_1_addr),
    .D_Out(memoryaccess_stage_1_d_out), .Funct3_Out(memoryaccess_stage_1_funct3_out),
    .RD(memoryaccess_stage_1_rd), .WR(memoryaccess_stage_1_wr));
  D_Memory d_memory_1 (
    .Addr(memoryaccess_stage_1_addr), .Data_In(memoryaccess_stage_1_d_out),
    .Funct3(memoryaccess_stage_1_funct3_out), .WR(memoryaccess_stage_1_wr), .RD(memoryaccess_stage_1_rd),
    .Clk(clock_1_out), .Data_Out(d_memory_1_data_out));
  MEM_WB_Reg mem_wb_reg_1 (
    .M_Result_In(memoryaccess_stage_1_m_result_out), .Imm_In(memoryaccess_stage_1_imm_out), .WE(1'b1),
    .Clk(clock_1_out), .Reset(in_1), .PC_In(memoryaccess_stage_1_pc_out),
    .Next_PC_In(memoryaccess_stage_1_next_pc_out), .WB_In(memoryaccess_stage_1_wb_out),
    .WB_Sel_In(memoryaccess_stage_1_wb_sel_out), .RD_Sel_In(memoryaccess_stage_1_rd_sel_out),
    .A_Result_In(memoryaccess_stage_1_a_result_out), .M_Result_Out(mem_wb_reg_1_m_result_out),
    .Imm_Out(mem_wb_reg_1_imm_out), .PC_Out(mem_wb_reg_1_pc_out), .Next_PC_Out(mem_wb_reg_1_next_pc_out),
    .WB_Out(mem_wb_reg_1_wb_out), .WB_Sel_Out(mem_wb_reg_1_wb_sel_out), .RD_Sel_Out(mem_wb_reg_1_rd_sel_out),
    .A_Result_Out(mem_wb_reg_1_a_result_out));
  WriteBack_Stage writeback_stage_1 (
    .PC_In(mem_wb_reg_1_pc_out), .Next_PC_In(mem_wb_reg_1_next_pc_out), .WB_In(mem_wb_reg_1_wb_out),
    .WB_Sel_In(mem_wb_reg_1_wb_sel_out), .RD_Sel_In(mem_wb_reg_1_rd_sel_out),
    .A_Result_In(mem_wb_reg_1_a_result_out), .M_Result_In(mem_wb_reg_1_m_result_out),
    .Imm_In(mem_wb_reg_1_imm_out), .WB_Out(writeback_stage_1_wb_out),
    .RD_Sel_Out(writeback_stage_1_rd_sel_out), .Result(writeback_stage_1_result));
endmodule

module PC (
  input  [31:0] PC_In,
  input  PC_Select,
  input  Stall,
  input  Clk,
  input  Reset,
  output [31:0] PC_Out,
  output [31:0] Next_PC
);

  wire [31:0] multiplexer_1_out;

  Adder #(.width(32)) adder_1 (.a(PC_Out), .b(32'h4), .out(Next_PC));  // open: cin, cout
  Multiplexer #(.select(2), .width(32)) multiplexer_1 (
    .in0(Next_PC), .in1(PC_In), .in2(PC_Out), .in3(PC_Out), .out(multiplexer_1_out), .sel({Stall, PC_Select}));
  D_Flip_Flop d_ff_1 (.D(multiplexer_1_out[0]), .clk(Clk), .Q(PC_Out[0]), .reset(Reset));  // open: Qn, preset
  D_Flip_Flop d_ff_2 (.D(multiplexer_1_out[1]), .clk(Clk), .Q(PC_Out[1]), .reset(Reset));  // open: Qn, preset
  D_Flip_Flop d_ff_3 (.D(multiplexer_1_out[2]), .clk(Clk), .Q(PC_Out[2]), .preset(Reset));  // open: Qn, reset
  D_Flip_Flop d_ff_4 (.D(multiplexer_1_out[3]), .clk(Clk), .Q(PC_Out[3]), .preset(Reset));  // open: Qn, reset
  D_Flip_Flop d_ff_5 (.D(multiplexer_1_out[4]), .clk(Clk), .Q(PC_Out[4]), .preset(Reset));  // open: Qn, reset
  D_Flip_Flop d_ff_6 (.D(multiplexer_1_out[5]), .clk(Clk), .Q(PC_Out[5]), .preset(Reset));  // open: Qn, reset
  D_Flip_Flop d_ff_7 (.D(multiplexer_1_out[6]), .clk(Clk), .Q(PC_Out[6]), .preset(Reset));  // open: Qn, reset
  D_Flip_Flop d_ff_8 (.D(multiplexer_1_out[7]), .clk(Clk), .Q(PC_Out[7]), .preset(Reset));  // open: Qn, reset
  D_Flip_Flop d_ff_9 (.D(multiplexer_1_out[8]), .clk(Clk), .Q(PC_Out[8]), .preset(Reset));  // open: Qn, reset
  D_Flip_Flop d_ff_10 (.D(multiplexer_1_out[9]), .clk(Clk), .Q(PC_Out[9]), .preset(Reset));  // open: Qn, reset
  D_Flip_Flop d_ff_11 (.D(multiplexer_1_out[10]), .clk(Clk), .Q(PC_Out[10]), .preset(Reset));  // open: Qn, reset
  D_Flip_Flop d_ff_12 (.D(multiplexer_1_out[11]), .clk(Clk), .Q(PC_Out[11]), .preset(Reset));  // open: Qn, reset
  D_Flip_Flop d_ff_13 (.D(multiplexer_1_out[12]), .clk(Clk), .Q(PC_Out[12]), .preset(Reset));  // open: Qn, reset
  D_Flip_Flop d_ff_14 (.D(multiplexer_1_out[13]), .clk(Clk), .Q(PC_Out[13]), .preset(Reset));  // open: Qn, reset
  D_Flip_Flop d_ff_15 (.D(multiplexer_1_out[14]), .clk(Clk), .Q(PC_Out[14]), .preset(Reset));  // open: Qn, reset
  D_Flip_Flop d_ff_16 (.D(multiplexer_1_out[15]), .clk(Clk), .Q(PC_Out[15]), .preset(Reset));  // open: Qn, reset
  D_Flip_Flop d_ff_17 (.D(multiplexer_1_out[16]), .clk(Clk), .Q(PC_Out[16]), .preset(Reset));  // open: Qn, reset
  D_Flip_Flop d_ff_18 (.D(multiplexer_1_out[17]), .clk(Clk), .Q(PC_Out[17]), .preset(Reset));  // open: Qn, reset
  D_Flip_Flop d_ff_19 (.D(multiplexer_1_out[18]), .clk(Clk), .Q(PC_Out[18]), .preset(Reset));  // open: Qn, reset
  D_Flip_Flop d_ff_20 (.D(multiplexer_1_out[19]), .clk(Clk), .Q(PC_Out[19]), .preset(Reset));  // open: Qn, reset
  D_Flip_Flop d_ff_21 (.D(multiplexer_1_out[20]), .clk(Clk), .Q(PC_Out[20]), .preset(Reset));  // open: Qn, reset
  D_Flip_Flop d_ff_22 (.D(multiplexer_1_out[21]), .clk(Clk), .Q(PC_Out[21]), .preset(Reset));  // open: Qn, reset
  D_Flip_Flop d_ff_23 (.D(multiplexer_1_out[22]), .clk(Clk), .Q(PC_Out[22]), .preset(Reset));  // open: Qn, reset
  D_Flip_Flop d_ff_24 (.D(multiplexer_1_out[23]), .clk(Clk), .Q(PC_Out[23]), .preset(Reset));  // open: Qn, reset
  D_Flip_Flop d_ff_25 (.D(multiplexer_1_out[24]), .clk(Clk), .Q(PC_Out[24]), .preset(Reset));  // open: Qn, reset
  D_Flip_Flop d_ff_26 (.D(multiplexer_1_out[25]), .clk(Clk), .Q(PC_Out[25]), .preset(Reset));  // open: Qn, reset
  D_Flip_Flop d_ff_27 (.D(multiplexer_1_out[26]), .clk(Clk), .Q(PC_Out[26]), .preset(Reset));  // open: Qn, reset
  D_Flip_Flop d_ff_28 (.D(multiplexer_1_out[27]), .clk(Clk), .Q(PC_Out[27]), .preset(Reset));  // open: Qn, reset
  D_Flip_Flop d_ff_29 (.D(multiplexer_1_out[28]), .clk(Clk), .Q(PC_Out[28]), .preset(Reset));  // open: Qn, reset
  D_Flip_Flop d_ff_30 (.D(multiplexer_1_out[29]), .clk(Clk), .Q(PC_Out[29]), .preset(Reset));  // open: Qn, reset
  D_Flip_Flop d_ff_31 (.D(multiplexer_1_out[30]), .clk(Clk), .Q(PC_Out[30]), .preset(Reset));  // open: Qn, reset
  D_Flip_Flop d_ff_32 (.D(multiplexer_1_out[31]), .clk(Clk), .Q(PC_Out[31]), .preset(Reset));  // open: Qn, reset
endmodule

module Instr_Reg (
  input  [31:0] D,
  input  WE,
  input  Clk,
  input  Reset,
  output [31:0] Q
);

  wire and_1_out, and_2_out, and_3_out, and_4_out, and_5_out, and_6_out, and_7_out, and_8_out, and_9_out,
       and_10_out, or_1_out, or_2_out, or_3_out, or_4_out, or_5_out;

  and and_1 (and_1_out, D[4], WE);
  and and_2 (and_2_out, ~WE, Q[4]);  // AND_Gate
  and and_3 (and_3_out, D[3], WE);
  and and_4 (and_4_out, ~WE, Q[3]);  // AND_Gate
  and and_5 (and_5_out, D[2], WE);
  and and_6 (and_6_out, ~WE, Q[2]);  // AND_Gate
  and and_7 (and_7_out, D[1], WE);
  and and_8 (and_8_out, ~WE, Q[1]);  // AND_Gate
  and and_9 (and_9_out, D[0], WE);
  and and_10 (and_10_out, ~WE, Q[0]);  // AND_Gate
  Register #(.width(27)) register_1 (.D(D[31:5]), .en(WE), .clk(Clk), .Q(Q[31:5]), .clr(Reset));
  D_Flip_Flop d_ff_1 (.D(or_1_out), .clk(Clk), .Q(Q[4]), .preset(Reset));  // open: Qn, reset
  or or_1 (or_1_out, and_1_out, and_2_out);
  D_Flip_Flop d_ff_2 (.D(or_2_out), .clk(Clk), .Q(Q[3]), .reset(Reset));  // open: Qn, preset
  or or_2 (or_2_out, and_3_out, and_4_out);
  D_Flip_Flop d_ff_3 (.D(or_3_out), .clk(Clk), .Q(Q[2]), .reset(Reset));  // open: Qn, preset
  or or_3 (or_3_out, and_5_out, and_6_out);
  D_Flip_Flop d_ff_4 (.D(or_4_out), .clk(Clk), .Q(Q[1]), .preset(Reset));  // open: Qn, reset
  or or_4 (or_4_out, and_7_out, and_8_out);
  D_Flip_Flop d_ff_5 (.D(or_5_out), .clk(Clk), .Q(Q[0]), .preset(Reset));  // open: Qn, reset
  or or_5 (or_5_out, and_9_out, and_10_out);
  // Probe on Q
endmodule

module Reg_File (
  input  [31:0] D,
  input  WE,
  input  [4:0] RD_Sel,
  input  [4:0] RS1_Sel,
  input  Clk,
  input  Reset,
  input  [4:0] RS2_Sel,
  output [31:0] RS1,
  output [31:0] RS2
);

  wire WE_01, WE_02, WE_03, WE_04, WE_05, WE_06, WE_07, WE_08, WE_09, WE_10, WE_11, WE_12, WE_13, WE_14,
       WE_15, WE_16, WE_17, WE_18, WE_19, WE_20, WE_21, WE_22, WE_23, WE_24, WE_25, WE_26, WE_27, WE_28,
       WE_29, WE_30, WE_31;
  wire [31:0] Q_01, Q_02, Q_03, Q_04, Q_05, Q_06, Q_07, Q_08, Q_09, Q_10, Q_11, Q_12, Q_13, Q_14, Q_15, Q_16,
       Q_17, Q_18, Q_19, Q_20, Q_21, Q_22, Q_23, Q_24, Q_25, Q_26, Q_27, Q_28, Q_29, Q_30, Q_31;

  Demultiplexer #(.select(5)) demultiplexer_1 (
    .out1(WE_01), .out2(WE_02), .out3(WE_03), .out4(WE_04), .out5(WE_05), .out6(WE_06), .out7(WE_07),
    .out8(WE_08), .out9(WE_09), .out10(WE_10), .out11(WE_11), .out12(WE_12), .out13(WE_13), .out14(WE_14),
    .out15(WE_15), .out16(WE_16), .out17(WE_17), .out18(WE_18), .out19(WE_19), .out20(WE_20), .out21(WE_21),
    .out22(WE_22), .out23(WE_23), .out24(WE_24), .out25(WE_25), .out26(WE_26), .out27(WE_27), .out28(WE_28),
    .out29(WE_29), .out30(WE_30), .out31(WE_31), .in(WE), .sel(RD_Sel));  // open: out0
  Register #(.width(32)) register_1 (.D(D), .en(WE_01), .clk(Clk), .Q(Q_01), .clr(Reset));
  Register #(.width(32)) register_2 (.D(D), .en(WE_02), .clk(Clk), .Q(Q_02), .clr(Reset));
  Register #(.width(32)) register_3 (.D(D), .en(WE_03), .clk(Clk), .Q(Q_03), .clr(Reset));
  Register #(.width(32)) register_4 (.D(D), .en(WE_04), .clk(Clk), .Q(Q_04), .clr(Reset));
  Register #(.width(32)) register_5 (.D(D), .en(WE_05), .clk(Clk), .Q(Q_05), .clr(Reset));
  Register #(.width(32)) register_6 (.D(D), .en(WE_06), .clk(Clk), .Q(Q_06), .clr(Reset));
  Register #(.width(32)) register_7 (.D(D), .en(WE_07), .clk(Clk), .Q(Q_07), .clr(Reset));
  Register #(.width(32)) register_8 (.D(D), .en(WE_08), .clk(Clk), .Q(Q_08), .clr(Reset));
  Register #(.width(32)) register_9 (.D(D), .en(WE_09), .clk(Clk), .Q(Q_09), .clr(Reset));
  Register #(.width(32)) register_10 (.D(D), .en(WE_10), .clk(Clk), .Q(Q_10), .clr(Reset));
  Register #(.width(32)) register_11 (.D(D), .en(WE_11), .clk(Clk), .Q(Q_11), .clr(Reset));
  Register #(.width(32)) register_12 (.D(D), .en(WE_12), .clk(Clk), .Q(Q_12), .clr(Reset));
  Register #(.width(32)) register_13 (.D(D), .en(WE_13), .clk(Clk), .Q(Q_13), .clr(Reset));
  Register #(.width(32)) register_14 (.D(D), .en(WE_14), .clk(Clk), .Q(Q_14), .clr(Reset));
  Register #(.width(32)) register_15 (.D(D), .en(WE_15), .clk(Clk), .Q(Q_15), .clr(Reset));
  Register #(.width(32)) register_16 (.D(D), .en(WE_16), .clk(Clk), .Q(Q_16), .clr(Reset));
  Register #(.width(32)) register_17 (.D(D), .en(WE_17), .clk(Clk), .Q(Q_17), .clr(Reset));
  Register #(.width(32)) register_18 (.D(D), .en(WE_18), .clk(Clk), .Q(Q_18), .clr(Reset));
  Register #(.width(32)) register_19 (.D(D), .en(WE_19), .clk(Clk), .Q(Q_19), .clr(Reset));
  Register #(.width(32)) register_20 (.D(D), .en(WE_20), .clk(Clk), .Q(Q_20), .clr(Reset));
  Register #(.width(32)) register_21 (.D(D), .en(WE_21), .clk(Clk), .Q(Q_21), .clr(Reset));
  Register #(.width(32)) register_22 (.D(D), .en(WE_22), .clk(Clk), .Q(Q_22), .clr(Reset));
  Register #(.width(32)) register_23 (.D(D), .en(WE_23), .clk(Clk), .Q(Q_23), .clr(Reset));
  Register #(.width(32)) register_24 (.D(D), .en(WE_24), .clk(Clk), .Q(Q_24), .clr(Reset));
  Register #(.width(32)) register_25 (.D(D), .en(WE_25), .clk(Clk), .Q(Q_25), .clr(Reset));
  Register #(.width(32)) register_26 (.D(D), .en(WE_26), .clk(Clk), .Q(Q_26), .clr(Reset));
  Register #(.width(32)) register_27 (.D(D), .en(WE_27), .clk(Clk), .Q(Q_27), .clr(Reset));
  Register #(.width(32)) register_28 (.D(D), .en(WE_28), .clk(Clk), .Q(Q_28), .clr(Reset));
  Register #(.width(32)) register_29 (.D(D), .en(WE_29), .clk(Clk), .Q(Q_29), .clr(Reset));
  Register #(.width(32)) register_30 (.D(D), .en(WE_30), .clk(Clk), .Q(Q_30), .clr(Reset));
  Register #(.width(32)) register_31 (.D(D), .en(WE_31), .clk(Clk), .Q(Q_31), .clr(Reset));
  Multiplexer #(.select(5), .width(32)) multiplexer_1 (
    .in0({32{1'b0}}), .in1(Q_01), .in2(Q_02), .in3(Q_03), .in4(Q_04), .in5(Q_05), .in6(Q_06), .in7(Q_07),
    .in8(Q_08), .in9(Q_09), .in10(Q_10), .in11(Q_11), .in12(Q_12), .in13(Q_13), .in14(Q_14), .in15(Q_15),
    .in16(Q_16), .in17(Q_17), .in18(Q_18), .in19(Q_19), .in20(Q_20), .in21(Q_21), .in22(Q_22), .in23(Q_23),
    .in24(Q_24), .in25(Q_25), .in26(Q_26), .in27(Q_27), .in28(Q_28), .in29(Q_29), .in30(Q_30), .in31(Q_31),
    .out(RS1), .sel(RS1_Sel));
  Multiplexer #(.select(5), .width(32)) multiplexer_2 (
    .in0({32{1'b0}}), .in1(Q_01), .in2(Q_02), .in3(Q_03), .in4(Q_04), .in5(Q_05), .in6(Q_06), .in7(Q_07),
    .in8(Q_08), .in9(Q_09), .in10(Q_10), .in11(Q_11), .in12(Q_12), .in13(Q_13), .in14(Q_14), .in15(Q_15),
    .in16(Q_16), .in17(Q_17), .in18(Q_18), .in19(Q_19), .in20(Q_20), .in21(Q_21), .in22(Q_22), .in23(Q_23),
    .in24(Q_24), .in25(Q_25), .in26(Q_26), .in27(Q_27), .in28(Q_28), .in29(Q_29), .in30(Q_30), .in31(Q_31),
    .out(RS2), .sel(RS2_Sel));
endmodule

module Imm_decoder (
  input  [31:0] Instr,
  output [31:0] Imm
);

  wire [31:0] B_Imm, I_Imm, J_Imm, S_Imm;

  assign I_Imm = {{20{Instr[31]}}, Instr[31:20]};  // Bit_Extender bit_extender_1
  assign S_Imm = {{20{Instr[31]}}, {Instr[31:25], Instr[11:7]}};  // Bit_Extender bit_extender_2
  assign B_Imm = {{19{Instr[31]}}, {Instr[31], Instr[7], Instr[30:25], Instr[11:8], 1'b0}};  // Bit_Extender bit_extender_3
  assign J_Imm = {{11{Instr[31]}}, {Instr[31], Instr[19:12], Instr[20], Instr[30:21], 1'b0}};  // Bit_Extender bit_extender_4
  Multiplexer #(.select(5), .width(32)) multiplexer_1 (
    .in0(I_Imm), .in1({32{1'b0}}), .in2({32{1'b0}}), .in3({32{1'b0}}), .in4(I_Imm),
    .in5({Instr[31:12], {12{1'b0}}}), .in6({32{1'b0}}), .in7({32{1'b0}}), .in8(S_Imm), .in9({32{1'b0}}),
    .in10({32{1'b0}}), .in11({32{1'b0}}), .in12(I_Imm), .in13({Instr[31:12], {12{1'b0}}}), .in14({32{1'b0}}),
    .in15({32{1'b0}}), .in16({32{1'b0}}), .in17({32{1'b0}}), .in18({32{1'b0}}), .in19({32{1'b0}}),
    .in20({32{1'b0}}), .in21({32{1'b0}}), .in22({32{1'b0}}), .in23({32{1'b0}}), .in24(B_Imm), .in25(J_Imm),
    .in26({32{1'b0}}), .in27(J_Imm), .in28({32{1'b0}}), .in29({32{1'b0}}), .in30({32{1'b0}}),
    .in31({32{1'b0}}), .out(Imm), .sel(Instr[6:2]));

  // Other names for the same wires on the sheet: S8_11[3:0] = Instr[11:8]; S7 = Instr[7]; S21_24[3:0] = Instr[24:21];
  //   U_Imm[31:12] = Instr[31:12]; S25_30[5:0] = Instr[30:25]; S20 = Instr[20]; S12_19[7:0] = Instr[19:12];
  //   S31 = Instr[31]; OPCODE[6:0] = Instr[6:0]
endmodule

module Reg_Decoder (
  input  [31:0] Instr,
  output [4:0] RS2_Sel,
  output [4:0] RS1_Sel,
  output [4:0] RD_Sel
);


  assign RD_Sel = Instr[11:7];
  assign RS1_Sel = Instr[19:15];
  assign RS2_Sel = Instr[24:20];
endmodule

module Funct_Decoder (
  input  [31:0] Instr,
  output [2:0] Funct3,
  output [6:0] Funct7
);


  assign Funct3 = Instr[14:12];
  assign Funct7 = Instr[31:25];
endmodule

module Control_Unit (
  input  [31:0] Instr,
  output Branch,
  output Jmp,
  output [1:0] WB_Sel,
  output WB,
  output S1_PC,
  output Imm,
  output Mem_R,
  output Mem_W
);

  wire WB_Alu, WB_Imm, WB_Mem, WB_Next_PC;

  Multiplexer #(.select(5), .width(11)) multiplexer_1 (
    .in0(11'h348), .in1({11{1'b0}}), .in2({11{1'b0}}), .in3({11{1'b0}}), .in4(11'h150), .in5(11'h1d0),
    .in6({11{1'b0}}), .in7({11{1'b0}}), .in8(11'h500), .in9({11{1'b0}}), .in10({11{1'b0}}),
    .in11({11{1'b0}}), .in12(11'h50), .in13(11'h160), .in14({11{1'b0}}), .in15({11{1'b0}}),
    .in16({11{1'b0}}), .in17({11{1'b0}}), .in18({11{1'b0}}), .in19({11{1'b0}}), .in20({11{1'b0}}),
    .in21({11{1'b0}}), .in22({11{1'b0}}), .in23({11{1'b0}}), .in24(11'h181), .in25(11'h106),
    .in26({11{1'b0}}), .in27(11'h186), .in28({11{1'b0}}), .in29({11{1'b0}}), .in30({11{1'b0}}),
    .in31({11{1'b0}}), .out({Mem_W, Mem_R, Imm, S1_PC, WB, WB_Imm, WB_Alu, WB_Mem, WB_Next_PC, Jmp, Branch}),
    .sel(Instr[6:2]));
  and and_1 (WB_Sel[1], ~WB_Next_PC, ~WB_Alu);  // AND_Gate
  and and_2 (WB_Sel[0], ~WB_Next_PC, ~WB_Mem);  // AND_Gate
endmodule

module ALU (
  input  [31:0] A,
  input  [31:0] B,
  input  [2:0] Funct3,
  input  [6:0] Funct7,
  input  Imm,
  input  Force_SUM,
  output [31:0] Y
);

  wire comparator_1_lt, comparator_2_lt, not_1_out;
  wire [31:0] adder_1_out, and_1_out, bit_extender_1_out, bit_extender_2_out, multiplexer_1_out,
       multiplexer_2_out, multiplexer_3_out, or_1_out, shifter_1_out, shifter_2_out, shifter_3_out,
       subtractor_1_out, xor_1_out;

  Adder #(.width(32)) adder_1 (.a(A), .b(B), .out(adder_1_out));  // open: cin, cout
  Subtractor #(.width(32)) subtractor_1 (.a(A), .b(B), .out(subtractor_1_out));  // open: bin, bout
  Shifter #(.width(32)) shifter_1 (.in(A), .\dist (B[4:0]), .out(shifter_1_out));
  Comparator #(.width(32)) comparator_1 (.a(A), .b(B), .lt(comparator_1_lt));  // open: gt, eq
  assign bit_extender_1_out = {{31{comparator_1_lt}}, comparator_1_lt};  // Bit_Extender bit_extender_1
  Comparator #(.mode("unsigned"), .width(32)) comparator_2 (.a(A), .b(B), .lt(comparator_2_lt));  // open: gt, eq
  assign bit_extender_2_out = {{31{comparator_2_lt}}, comparator_2_lt};  // Bit_Extender bit_extender_2
  assign xor_1_out = A ^ B;  // XOR_Gate xor_1, 32 bits wide
  Shifter #(.shift("lr"), .width(32)) shifter_2 (.in(A), .\dist (B[4:0]), .out(shifter_2_out));
  Multiplexer #(.width(32)) multiplexer_1 (
    .in0(shifter_2_out), .in1(shifter_3_out), .out(multiplexer_1_out), .sel(Funct7[5]));
  Shifter #(.shift("ar"), .width(32)) shifter_3 (.in(A), .\dist (B[4:0]), .out(shifter_3_out));
  assign or_1_out = A | B;  // OR_Gate or_1, 32 bits wide
  assign and_1_out = A & B;  // AND_Gate and_1, 32 bits wide
  Multiplexer #(.select(2), .width(32)) multiplexer_2 (
    .in0(adder_1_out), .in1(subtractor_1_out), .in2(adder_1_out), .in3(adder_1_out), .out(multiplexer_2_out),
    .sel({Imm, Funct7[5]}));
  Multiplexer #(.select(3), .width(32)) multiplexer_3 (
    .in0(multiplexer_2_out), .in1(shifter_1_out), .in2(bit_extender_1_out), .in3(bit_extender_2_out),
    .in4(xor_1_out), .in5(multiplexer_1_out), .in6(or_1_out), .in7(and_1_out), .out(multiplexer_3_out),
    .sel(Funct3));
  not not_1 (not_1_out, Force_SUM);
  Multiplexer #(.width(32)) multiplexer_4 (.in0(adder_1_out), .in1(multiplexer_3_out), .out(Y), .sel(not_1_out));
endmodule

module IF_ID_Reg (
  input  [31:0] PC_In,
  input  [31:0] Next_PC_In,
  input  [31:0] Instr_In,
  input  Stall,
  input  Clk,
  input  Reset,
  output [31:0] PC_Out,
  output [31:0] Next_PC_Out,
  output [31:0] Instr_Out
);

  wire not_1_out, not_2_out;
  wire [31:0] Instr_q;

  not not_1 (not_1_out, Stall);
  Register #(.trigger("falling"), .width(32)) PC (.D(PC_In), .en(not_1_out), .clk(Clk), .Q(PC_Out), .clr(Reset));
  Register #(.trigger("falling"), .width(32)) Next_PC (
    .D(Next_PC_In), .en(not_1_out), .clk(Clk), .Q(Next_PC_Out), .clr(Reset));
  Instr_Reg Instr (.WE(not_1_out), .Clk(not_2_out), .Reset(Reset), .D(Instr_In), .Q(Instr_q));
  not not_2 (not_2_out, Clk);
  Multiplexer #(.width(32)) multiplexer_1 (.in0(32'h13), .in1(Instr_q), .out(Instr_Out), .sel(not_1_out));
endmodule

module ID_EX_Reg (
  input  [31:0] PC_In,
  input  [31:0] Next_PC_In,
  input  Jump_In,
  input  Branch_In,
  input  S1_Sel_In,
  input  S2_Sel_In,
  input  Mem_RD_In,
  input  Mem_WR_In,
  input  WB_In,
  input  [1:0] WB_Sel_In,
  input  [2:0] Funct3_In,
  input  [6:0] Funct7_In,
  input  [4:0] RS1_Sel_In,
  input  [4:0] RS2_Sel_In,
  input  [4:0] RD_Sel_In,
  input  [31:0] RS1_In,
  input  [31:0] RS2_In,
  input  [31:0] Imm_In,
  input  Stall,
  input  Clk,
  input  Reset,
  output [31:0] PC_Out,
  output [31:0] Next_PC_Out,
  output Jump_Out,
  output Branch_Out,
  output S1_Sel_Out,
  output S2_Sel_Out,
  output Mem_RD_Out,
  output Mem_WR_Out,
  output WB_Out,
  output [1:0] WB_Sel_Out,
  output [2:0] Funct3_Out,
  output [6:0] Funct7_Out,
  output [4:0] RS1_Sel_Out,
  output [4:0] RS2_Sel_Out,
  output [4:0] RD_Sel_Out,
  output [31:0] RS1_Out,
  output [31:0] RS2_Out,
  output [31:0] Imm_Out
);

  wire Branch_q, Jump_q, Mem_RD_q, Mem_WR_q, not_1_out, S1_Sel_q, S2_Sel_q, WB_q;

  not not_1 (not_1_out, Stall);
  Register #(.trigger("falling"), .width(32)) PC (.D(PC_In), .en(not_1_out), .clk(Clk), .Q(PC_Out), .clr(Reset));
  Register #(.trigger("falling"), .width(32)) Next_PC (
    .D(Next_PC_In), .en(not_1_out), .clk(Clk), .Q(Next_PC_Out), .clr(Reset));
  Register #(.trigger("falling"), .width(1)) Jump (.D(Jump_In), .en(not_1_out), .clk(Clk), .Q(Jump_q), .clr(Reset));
  Register #(.trigger("falling"), .width(1)) Branch (
    .D(Branch_In), .en(not_1_out), .clk(Clk), .Q(Branch_q), .clr(Reset));
  Register #(.trigger("falling"), .width(1)) S1_Sel (
    .D(S1_Sel_In), .en(not_1_out), .clk(Clk), .Q(S1_Sel_q), .clr(Reset));
  Register #(.trigger("falling"), .width(1)) S2_Sel (
    .D(S2_Sel_In), .en(not_1_out), .clk(Clk), .Q(S2_Sel_q), .clr(Reset));
  Register #(.trigger("falling"), .width(1)) Mem_RD (
    .D(Mem_RD_In), .en(not_1_out), .clk(Clk), .Q(Mem_RD_q), .clr(Reset));
  Register #(.trigger("falling"), .width(1)) Mem_WR (
    .D(Mem_WR_In), .en(not_1_out), .clk(Clk), .Q(Mem_WR_q), .clr(Reset));
  Register #(.trigger("falling"), .width(1)) WB (.D(WB_In), .en(not_1_out), .clk(Clk), .Q(WB_q), .clr(Reset));
  Register #(.trigger("falling"), .width(2)) WB_Sel (
    .D(WB_Sel_In), .en(not_1_out), .clk(Clk), .Q(WB_Sel_Out), .clr(Reset));
  Register #(.trigger("falling"), .width(3)) Funct3 (
    .D(Funct3_In), .en(not_1_out), .clk(Clk), .Q(Funct3_Out), .clr(Reset));
  Register #(.trigger("falling"), .width(7)) Funct7 (
    .D(Funct7_In), .en(not_1_out), .clk(Clk), .Q(Funct7_Out), .clr(Reset));
  Register #(.trigger("falling"), .width(5)) RS1_Sel (
    .D(RS1_Sel_In), .en(not_1_out), .clk(Clk), .Q(RS1_Sel_Out), .clr(Reset));
  Register #(.trigger("falling"), .width(5)) RS2_Sel (
    .D(RS2_Sel_In), .en(not_1_out), .clk(Clk), .Q(RS2_Sel_Out), .clr(Reset));
  Register #(.trigger("falling"), .width(5)) RD_Sel (
    .D(RD_Sel_In), .en(not_1_out), .clk(Clk), .Q(RD_Sel_Out), .clr(Reset));
  Register #(.trigger("falling"), .width(32)) RS1 (.D(RS1_In), .en(not_1_out), .clk(Clk), .Q(RS1_Out), .clr(Reset));
  Register #(.trigger("falling"), .width(32)) RS2 (.D(RS2_In), .en(not_1_out), .clk(Clk), .Q(RS2_Out), .clr(Reset));
  Register #(.trigger("falling"), .width(32)) Imm (.D(Imm_In), .en(not_1_out), .clk(Clk), .Q(Imm_Out), .clr(Reset));
  and and_1 (Jump_Out, Jump_q, not_1_out);
  and and_2 (Branch_Out, Branch_q, not_1_out);
  and and_3 (S1_Sel_Out, S1_Sel_q, not_1_out);
  and and_4 (S2_Sel_Out, S2_Sel_q, not_1_out);
  and and_5 (Mem_RD_Out, Mem_RD_q, not_1_out);
  and and_6 (Mem_WR_Out, Mem_WR_q, not_1_out);
  and and_7 (WB_Out, WB_q, not_1_out);
endmodule

module EX_MEM_Reg (
  input  [31:0] PC_In,
  input  [31:0] Next_PC_In,
  input  Mem_RD_In,
  input  Mem_WR_In,
  input  WB_In,
  input  [1:0] WB_Sel_In,
  input  [2:0] Funct3_In,
  input  [4:0] RS2_Sel_In,
  input  [4:0] RD_Sel_In,
  input  [31:0] RS2_In,
  input  [31:0] Result_In,
  input  [31:0] Imm_In,
  input  WE,
  input  Clk,
  input  Reset,
  output [31:0] PC_Out,
  output [31:0] Next_PC_Out,
  output Mem_RD_Out,
  output Mem_WR_Out,
  output WB_Out,
  output [1:0] WB_Sel_Out,
  output [2:0] Funct3_Out,
  output [4:0] RS2_Sel_Out,
  output [4:0] RD_Sel_Out,
  output [31:0] RS2_Out,
  output [31:0] Result_Out,
  output [31:0] Imm_Out
);

  Register #(.trigger("falling"), .width(32)) PC (.D(PC_In), .en(WE), .clk(Clk), .Q(PC_Out), .clr(Reset));
  Register #(.trigger("falling"), .width(32)) Next_PC (
    .D(Next_PC_In), .en(WE), .clk(Clk), .Q(Next_PC_Out), .clr(Reset));
  Register #(.trigger("falling"), .width(1)) Mem_RD (.D(Mem_RD_In), .en(WE), .clk(Clk), .Q(Mem_RD_Out), .clr(Reset));
  Register #(.trigger("falling"), .width(1)) Mem_WR (.D(Mem_WR_In), .en(WE), .clk(Clk), .Q(Mem_WR_Out), .clr(Reset));
  Register #(.trigger("falling"), .width(1)) WB (.D(WB_In), .en(WE), .clk(Clk), .Q(WB_Out), .clr(Reset));
  Register #(.trigger("falling"), .width(2)) WB_Sel (.D(WB_Sel_In), .en(WE), .clk(Clk), .Q(WB_Sel_Out), .clr(Reset));
  Register #(.trigger("falling"), .width(3)) Funct3 (.D(Funct3_In), .en(WE), .clk(Clk), .Q(Funct3_Out), .clr(Reset));
  Register #(.trigger("falling"), .width(5)) RS2_Sel (.D(RS2_Sel_In), .en(WE), .clk(Clk), .Q(RS2_Sel_Out), .clr(Reset));
  Register #(.trigger("falling"), .width(5)) RD_Sel (.D(RD_Sel_In), .en(WE), .clk(Clk), .Q(RD_Sel_Out), .clr(Reset));
  Register #(.trigger("falling"), .width(32)) RS2 (.D(RS2_In), .en(WE), .clk(Clk), .Q(RS2_Out), .clr(Reset));
  Register #(.trigger("falling"), .width(32)) Result (.D(Result_In), .en(WE), .clk(Clk), .Q(Result_Out), .clr(Reset));
  Register #(.trigger("falling"), .width(32)) Imm (.D(Imm_In), .en(WE), .clk(Clk), .Q(Imm_Out), .clr(Reset));
endmodule

module MEM_WB_Reg (
  input  [31:0] PC_In,
  input  [31:0] Next_PC_In,
  input  WB_In,
  input  [1:0] WB_Sel_In,
  input  [4:0] RD_Sel_In,
  input  [31:0] A_Result_In,
  input  [31:0] M_Result_In,
  input  [31:0] Imm_In,
  input  WE,
  input  Clk,
  input  Reset,
  output [31:0] PC_Out,
  output [31:0] Next_PC_Out,
  output WB_Out,
  output [1:0] WB_Sel_Out,
  output [4:0] RD_Sel_Out,
  output [31:0] A_Result_Out,
  output [31:0] M_Result_Out,
  output [31:0] Imm_Out
);

  Register #(.trigger("falling"), .width(32)) PC (.D(PC_In), .en(WE), .clk(Clk), .Q(PC_Out), .clr(Reset));
  Register #(.trigger("falling"), .width(32)) Next_PC (
    .D(Next_PC_In), .en(WE), .clk(Clk), .Q(Next_PC_Out), .clr(Reset));
  Register #(.trigger("falling"), .width(1)) WB (.D(WB_In), .en(WE), .clk(Clk), .Q(WB_Out), .clr(Reset));
  Register #(.trigger("falling"), .width(2)) WB_Sel (.D(WB_Sel_In), .en(WE), .clk(Clk), .Q(WB_Sel_Out), .clr(Reset));
  Register #(.trigger("falling"), .width(5)) RD_Sel (.D(RD_Sel_In), .en(WE), .clk(Clk), .Q(RD_Sel_Out), .clr(Reset));
  Register #(.trigger("falling"), .width(32)) A_Result (
    .D(A_Result_In), .en(WE), .clk(Clk), .Q(A_Result_Out), .clr(Reset));
  Register #(.trigger("falling"), .width(32)) M_Result (
    .D(M_Result_In), .en(WE), .clk(Clk), .Q(M_Result_Out), .clr(Reset));
  Register #(.trigger("falling"), .width(32)) Imm (.D(Imm_In), .en(WE), .clk(Clk), .Q(Imm_Out), .clr(Reset));
endmodule

module D_Memory (
  input  [31:0] Addr,
  input  [31:0] Data_In,
  input  [2:0] Funct3,
  input  WR,
  input  RD,
  input  Clk,
  output [31:0] Data_Out
);

  wire [1:0] multiplexer_1_out;
  wire [3:0] multiplexer_2_out, shifter_1_out;
  wire [7:0] multiplexer_3_out;
  wire [15:0] multiplexer_4_out, ram_1_dout, ram_1_dout_2;
  wire [31:0] bit_extender_1_out, bit_extender_2_out, bit_extender_3_out, bit_extender_4_out, shifter_2_out;

  Multiplexer #(.select(2), .width(2)) multiplexer_1 (
    .in0(Addr[1:0]), .in1({Addr[1], 1'b0}), .in2(2'b00), .in3(2'b00), .out(multiplexer_1_out),
    .sel(Funct3[1:0]));
  Multiplexer #(.select(2), .width(4)) multiplexer_2 (
    .in0(4'b0001), .in1(4'b0011), .in2(4'b1111), .in3(4'b0000), .out(multiplexer_2_out), .sel(Funct3[1:0]));
  Shifter #(.width(4)) shifter_1 (.in(multiplexer_2_out), .\dist (multiplexer_1_out), .out(shifter_1_out));
  Shifter #(.width(32)) shifter_2 (.in(Data_In), .\dist ({multiplexer_1_out, 3'b000}), .out(shifter_2_out));
  RAM #(.addrWidth(24), .byteenables("byteEnables"), .dataWidth(32)) ram_1 (
    .addr(Addr[25:2]), .we(WR), .oe(RD), .clk(Clk), .din(shifter_2_out), .dout({ram_1_dout_2, ram_1_dout}),
    .be3(shifter_1_out[3]), .be2(shifter_1_out[2]), .be1(shifter_1_out[1]), .be0(shifter_1_out[0]));
  Multiplexer #(.select(2), .width(8)) multiplexer_3 (
    .in0(ram_1_dout[7:0]), .in1(ram_1_dout[15:8]), .in2(ram_1_dout_2[7:0]), .in3(ram_1_dout_2[15:8]),
    .out(multiplexer_3_out), .sel(Addr[1:0]));
  Multiplexer #(.select(2), .width(16)) multiplexer_4 (
    .in0(ram_1_dout), .in1(ram_1_dout), .in2(ram_1_dout_2), .in3(ram_1_dout_2), .out(multiplexer_4_out),
    .sel(Addr[1:0]));
  assign bit_extender_1_out = {{24{multiplexer_3_out[7]}}, multiplexer_3_out};  // Bit_Extender bit_extender_1
  assign bit_extender_2_out = {{24{1'b0}}, multiplexer_3_out};  // Bit_Extender bit_extender_2
  assign bit_extender_3_out = {{16{multiplexer_4_out[15]}}, multiplexer_4_out};  // Bit_Extender bit_extender_3
  assign bit_extender_4_out = {{16{1'b0}}, multiplexer_4_out};  // Bit_Extender bit_extender_4
  Multiplexer #(.select(3), .width(32)) multiplexer_5 (
    .in0(bit_extender_1_out), .in1(bit_extender_3_out), .in2({ram_1_dout_2, ram_1_dout}),
    .in4(bit_extender_2_out), .in5(bit_extender_4_out), .out(Data_Out), .sel(Funct3));  // open: in3, in6, in7

  // Other names for the same wires on the sheet: A1_0[1:0] = Addr[1:0]; F3[2:0] = Funct3; F3_2[1:0] = Funct3[1:0]
endmodule

module I_Memory (
  input  [31:0] Addr,
  input  Clk,
  input  Reset,
  output [31:0] Instr,
  output Stall
);

  ROM #(.addrWidth(16), .dataWidth(32)) rom_1 (.addr(Addr[17:2]), .data(Instr));
  Multiplexer #(.select(2), .width(32)) multiplexer_1 ();  // open: in0, in1, in2, in3, out, sel

  assign Stall = 1'b0;

  // Notes on the sheet:
  //   contents of rom_1 (hex, n*v repeats v):
  //   10000297 28293 428313 2028393 28e03 11e0e13 1c38023 128293 138393 fe62c6e3 10000297 fdc28293 428313
  //   2028393 29e03 22e0e13 1c39023 228293 238393 fe62c6e3 10000297 fb828293 2028393 2ae03 33e0e13 1c3a023
  //   6f 65509*13
endmodule

module Forwarding_Unit (
  input  RD,
  input  Mem_WB,
  input  [4:0] Mem_Reg,
  input  [31:0] Mem_Data,
  input  WB_WB,
  input  [4:0] WB_Reg,
  input  [31:0] WB_Data,
  input  [4:0] EX_RS1,
  input  [4:0] EX_RS2,
  input  [4:0] MEM_RS,
  output Stall,
  output EX_RS1_Sel,
  output [31:0] EX_RS1_Data,
  output EX_RS2_Sel,
  output [31:0] EX_RS2_Data,
  output MEM_RS_Sel,
  output [31:0] MEM_RS_Data
);

  wire and_1_out, and_2_out, and_3_out, and_4_out, and_5_out, and_6_out, and_7_out, comparator_1_eq,
       comparator_2_eq, comparator_3_eq, comparator_4_eq, comparator_5_eq, comparator_6_eq, comparator_7_eq,
       comparator_8_eq, or_1_out, or_2_out, or_3_out, or_4_out, or_5_out;

  and and_1 (and_1_out, ~RD, Mem_WB);  // AND_Gate
  Comparator #(.mode("unsigned"), .width(5)) comparator_1 (
    .a(Mem_Reg), .b(EX_RS1), .eq(comparator_1_eq));  // open: gt, lt
  Comparator #(.mode("unsigned"), .width(5)) comparator_2 (
    .a(WB_Reg), .b(EX_RS1), .eq(comparator_2_eq));  // open: gt, lt
  Comparator #(.mode("unsigned"), .width(5)) comparator_3 (
    .a(Mem_Reg), .b(EX_RS2), .eq(comparator_3_eq));  // open: gt, lt
  Comparator #(.mode("unsigned"), .width(5)) comparator_4 (
    .a(WB_Reg), .b(EX_RS2), .eq(comparator_4_eq));  // open: gt, lt
  Comparator #(.mode("unsigned"), .width(5)) comparator_5 (
    .a(WB_Reg), .b(MEM_RS), .eq(comparator_5_eq));  // open: gt, lt
  Comparator #(.mode("unsigned"), .width(5)) comparator_6 (
    .a(MEM_RS), .b({5{1'b0}}), .eq(comparator_6_eq));  // open: gt, lt
  or or_1 (or_1_out, ~comparator_1_eq, ~and_1_out);  // OR_Gate
  or or_2 (or_2_out, ~comparator_3_eq, ~and_1_out);  // OR_Gate
  Multiplexer #(.width(32)) multiplexer_1 (.in0(Mem_Data), .in1(WB_Data), .out(EX_RS1_Data), .sel(or_1_out));
  Multiplexer #(.width(32)) multiplexer_2 (.in0(Mem_Data), .in1(WB_Data), .out(EX_RS2_Data), .sel(or_2_out));
  and and_2 (and_2_out, comparator_1_eq, and_1_out);
  or or_3 (or_3_out, and_2_out, and_3_out);
  and and_3 (and_3_out, WB_WB, comparator_2_eq);
  and and_4 (and_4_out, comparator_3_eq, and_1_out);
  or or_4 (or_4_out, and_4_out, and_5_out);
  and and_5 (and_5_out, WB_WB, comparator_4_eq);
  Comparator #(.mode("unsigned"), .width(5)) comparator_7 (
    .a(EX_RS1), .b({5{1'b0}}), .eq(comparator_7_eq));  // open: gt, lt
  Comparator #(.mode("unsigned"), .width(5)) comparator_8 (
    .a(EX_RS2), .b({5{1'b0}}), .eq(comparator_8_eq));  // open: gt, lt
  and and_6 (and_6_out, comparator_1_eq, ~comparator_7_eq);  // AND_Gate
  and and_7 (and_7_out, comparator_3_eq, ~comparator_8_eq);  // AND_Gate
  or or_5 (or_5_out, and_6_out, and_7_out);
  and and_8 (EX_RS1_Sel, or_3_out, ~comparator_7_eq);  // AND_Gate
  and and_9 (EX_RS2_Sel, or_4_out, ~comparator_8_eq);  // AND_Gate
  and and_10 (MEM_RS_Sel, WB_WB, comparator_5_eq, ~comparator_6_eq);  // AND_Gate
  and and_11 (Stall, RD, or_5_out);

  assign MEM_RS_Data = WB_Data;
endmodule

module Control_Transfer_Unit (
  input  Jump,
  input  Branch,
  input  [31:0] A,
  input  [31:0] B,
  input  [2:0] Funct3,
  input  Clk,
  input  Clk90,
  output PC_Sel,
  output Flush
);

  wire and_1_out, comparator_1_eq, comparator_1_lt, comparator_2_lt, multiplexer_1_out, not_1_out, not_2_out,
       not_3_out;

  Comparator #(.width(32)) comparator_1 (.a(A), .b(B), .eq(comparator_1_eq), .lt(comparator_1_lt));  // open: gt
  Comparator #(.mode("unsigned"), .width(32)) comparator_2 (.a(A), .b(B), .lt(comparator_2_lt));  // open: gt, eq
  not not_1 (not_1_out, comparator_1_eq);
  Multiplexer #(.select(3)) multiplexer_1 (
    .in0(comparator_1_eq), .in1(not_1_out), .in2(1'b0), .in3(1'b0), .in4(comparator_1_lt), .in5(not_2_out),
    .in6(comparator_2_lt), .in7(not_3_out), .out(multiplexer_1_out), .sel(Funct3));
  not not_2 (not_2_out, comparator_1_lt);
  not not_3 (not_3_out, comparator_2_lt);
  and and_1 (and_1_out, Branch, multiplexer_1_out);
  or or_1 (PC_Sel, Jump, and_1_out);
  and and_2 (Flush, PC_Sel, Clk, ~Clk90);  // AND_Gate
endmodule

module Fetch_Stage (
  input  [31:0] Branch_PC,
  input  PC_Sel,
  input  Stall,
  input  Clk,
  input  Reset,
  input  Mem_Stall,
  input  [31:0] Instr_In,
  output [31:0] PC_Out,
  output [31:0] Next_PC,
  output [31:0] Instr_Out,
  output [31:0] Address
);

  wire or_1_out;

  PC pc_1 (
    .PC_In(Branch_PC), .PC_Select(PC_Sel), .Stall(or_1_out), .Clk(Clk), .Reset(Reset), .PC_Out(Address),
    .Next_PC(Next_PC));
  or or_1 (or_1_out, Stall, Mem_Stall);
  Multiplexer #(.width(32)) multiplexer_1 (.in0(Instr_In), .in1(32'h13), .out(Instr_Out), .sel(or_1_out));

  assign PC_Out = Address;
endmodule

module Decode_Stage (
  input  [31:0] PC_In,
  input  [31:0] Next_PC_In,
  input  [31:0] Instr_In,
  input  [31:0] D,
  input  [4:0] RD_Sel,
  input  WE,
  input  Clk,
  input  Reset,
  output [31:0] PC_Out,
  output [31:0] Next_PC_Out,
  output Jump_Out,
  output Branch_Out,
  output S1_Sel_Out,
  output S2_Sel_Out,
  output Mem_RD_Out,
  output Mem_WR_Out,
  output WB_Out,
  output [1:0] WB_Sel_Out,
  output [2:0] Funct3_Out,
  output [6:0] Funct7_Out,
  output [4:0] RS1_Sel_Out,
  output [4:0] RS2_Sel_Out,
  output [4:0] RD_Sel_Out,
  output [31:0] RS1_Out,
  output [31:0] RS2_Out,
  output [31:0] Imm_Out
);

  Control_Unit control_unit_1 (
    .Instr(Instr_In), .WB_Sel(WB_Sel_Out), .Branch(Branch_Out), .Jmp(Jump_Out), .WB(WB_Out),
    .S1_PC(S1_Sel_Out), .Imm(S2_Sel_Out), .Mem_R(Mem_RD_Out), .Mem_W(Mem_WR_Out));
  Funct_Decoder funct_decoder_1 (.Instr(Instr_In), .Funct3(Funct3_Out), .Funct7(Funct7_Out));
  Reg_Decoder reg_decoder_1 (.Instr(Instr_In), .RS2_Sel(RS2_Sel_Out), .RS1_Sel(RS1_Sel_Out), .RD_Sel(RD_Sel_Out));
  Reg_File reg_file_1 (
    .RS2_Sel(RS2_Sel_Out), .RS1_Sel(RS1_Sel_Out), .WE(WE), .RD_Sel(RD_Sel), .Clk(Clk), .Reset(Reset), .D(D),
    .RS2(RS2_Out), .RS1(RS1_Out));
  Imm_decoder imm_decoder_1 (.Instr(Instr_In), .Imm(Imm_Out));

  assign Next_PC_Out = Next_PC_In;
  assign PC_Out = PC_In;

  // Other names for the same wires on the sheet: Branch = Branch_Out; Funct3[2:0] = Funct3_Out;
  //   Funct7[6:0] = Funct7_Out; Imm[31:0] = Imm_Out; Instr[31:0] = Instr_In; Jump = Jump_Out; Mem_RD = Mem_RD_Out;
  //   Mem_WR = Mem_WR_Out; Next_PC[31:0] = Next_PC_In; PC[31:0] = PC_In; RD[4:0] = RD_Sel; RD_Sel_t[4:0] = RD_Sel_Out;
  //   RS1[31:0] = RS1_Out; RS1_Sel[4:0] = RS1_Sel_Out; RS2[31:0] = RS2_Out; RS2_Sel[4:0] = RS2_Sel_Out;
  //   S1_Sel = S1_Sel_Out; S2_Sel = S2_Sel_Out; WB = WB_Out; WB_Sel[1:0] = WB_Sel_Out
endmodule

module EX_Stage (
  input  [31:0] PC_In,
  input  [31:0] Next_PC_In,
  input  Jump_In,
  input  Branch_In,
  input  S1_Sel_In,
  input  S2_Sel_In,
  input  Mem_RD_In,
  input  Mem_WR_In,
  input  WB_In,
  input  [1:0] WB_Sel_In,
  input  [2:0] Funct3_In,
  input  [6:0] Funct7_In,
  input  [4:0] RS1_Sel_In,
  input  [4:0] RS2_Sel_In,
  input  [4:0] RD_Sel_In,
  input  [31:0] RS1_In,
  input  [31:0] RS2_In,
  input  [31:0] Imm_In,
  input  Clk,
  input  Clk90,
  output [31:0] PC_Out,
  output [31:0] Next_PC_Out,
  output Mem_RD_Out,
  output Mem_WR_Out,
  output WB_Out,
  output [1:0] WB_Sel_Out,
  output [2:0] Funct3_Out,
  output [4:0] RS2_Sel_Out,
  output [4:0] RD_Sel_Out,
  output [31:0] RS2_Out,
  output [31:0] Result_Out,
  output [31:0] Imm_Out,
  output PC_Sel,
  output Flush
);

  wire or_1_out;
  wire [31:0] multiplexer_1_out, multiplexer_2_out;

  Multiplexer #(.width(32)) multiplexer_1 (.in0(RS1_In), .in1(PC_In), .out(multiplexer_1_out), .sel(S1_Sel_In));
  Multiplexer #(.width(32)) multiplexer_2 (.in0(RS2_In), .in1(Imm_In), .out(multiplexer_2_out), .sel(S2_Sel_In));
  ALU alu_1 (
    .Funct3(Funct3_In), .Funct7(Funct7_In), .Imm(S2_Sel_In), .Force_SUM(or_1_out), .A(multiplexer_1_out),
    .B(multiplexer_2_out), .Y(Result_Out));
  or or_1 (or_1_out, Mem_WR_In, Mem_RD_In, Branch_In, Jump_In);
  Control_Transfer_Unit control_transfer_unit_1 (
    .Jump(Jump_In), .Branch(Branch_In), .Funct3(Funct3_In), .Clk(Clk), .Clk90(Clk90), .A(RS1_In), .B(RS2_In),
    .PC_Sel(PC_Sel), .Flush(Flush));

  assign Funct3_Out = Funct3_In;
  assign Imm_Out = Imm_In;
  assign Mem_RD_Out = Mem_RD_In;
  assign Mem_WR_Out = Mem_WR_In;
  assign Next_PC_Out = Next_PC_In;
  assign PC_Out = PC_In;
  assign RD_Sel_Out = RD_Sel_In;
  assign RS2_Out = RS2_In;
  assign RS2_Sel_Out = RS2_Sel_In;
  assign WB_Out = WB_In;
  assign WB_Sel_Out = WB_Sel_In;

  // Other names for the same wires on the sheet: Branch = Branch_In; Funct3[2:0] = Funct3_In; Funct7[6:0] = Funct7_In;
  //   Imm[31:0] = Imm_In; Jump = Jump_In; Mem_RD = Mem_RD_In; Mem_WR = Mem_WR_In; Next_PC[31:0] = Next_PC_In;
  //   PC[31:0] = PC_In; RD_Sel[4:0] = RD_Sel_In; Result[31:0] = Result_Out; RS1[31:0] = RS1_In;
  //   RS1_Sel[4:0] = RS1_Sel_In; RS2[31:0] = RS2_In; RS2_Sel[4:0] = RS2_Sel_In; S1_Sel = S1_Sel_In;
  //   S2_Sel = S2_Sel_In; WB = WB_In; WB_Sel[1:0] = WB_Sel_In
endmodule

module MemoryAccess_Stage (
  input  [31:0] PC_In,
  input  [31:0] Next_PC_In,
  input  Mem_RD_In,
  input  Mem_WR_In,
  input  WB_In,
  input  [1:0] WB_Sel_In,
  input  [2:0] Funct3_In,
  input  [4:0] RS2_Sel_In,
  input  [4:0] RD_Sel_In,
  input  [31:0] RS2_In,
  input  [31:0] Result_In,
  input  [31:0] Imm_In,
  input  [31:0] D_In,
  input  Mem_Stall,
  output [31:0] PC_Out,
  output [31:0] Next_PC_Out,
  output WB_Out,
  output [1:0] WB_Sel_Out,
  output [4:0] RD_Sel_Out,
  output [31:0] A_Result_Out,
  output [31:0] M_Result_Out,
  output [31:0] Imm_Out,
  output [31:0] Forward_D,
  output [31:0] Addr,
  output [31:0] D_Out,
  output [2:0] Funct3_Out,
  output RD,
  output WR
);

  Multiplexer #(.select(2), .width(32)) multiplexer_1 (
    .in0(Next_PC_In), .in1(Result_In), .in2({32{1'b0}}), .in3(Imm_In), .out(Forward_D), .sel(WB_Sel_In));

  assign A_Result_Out = Result_In;
  assign Addr = Result_In;
  assign D_Out = RS2_In;
  assign Funct3_Out = Funct3_In;
  assign Imm_Out = Imm_In;
  assign M_Result_Out = D_In;
  assign Next_PC_Out = Next_PC_In;
  assign PC_Out = PC_In;
  assign RD = Mem_RD_In;
  assign RD_Sel_Out = RD_Sel_In;
  assign WB_Out = WB_In;
  assign WB_Sel_Out = WB_Sel_In;
  assign WR = Mem_WR_In;

  // Other names for the same wires on the sheet: ALU_Result[31:0] = Result_In; Funct3[2:0] = Funct3_In;
  //   Imm[31:0] = Imm_In; Mem_RD = Mem_RD_In; Mem_Result[31:0] = D_In; Mem_WR = Mem_WR_In; Next_PC[31:0] = Next_PC_In;
  //   PC[31:0] = PC_In; RD_Sel[4:0] = RD_Sel_In; RS2[31:0] = RS2_In; RS2_Sel[4:0] = RS2_Sel_In; WB = WB_In;
  //   WB_Sel[1:0] = WB_Sel_In
endmodule

module WriteBack_Stage (
  input  [31:0] PC_In,
  input  [31:0] Next_PC_In,
  input  WB_In,
  input  [1:0] WB_Sel_In,
  input  [4:0] RD_Sel_In,
  input  [31:0] A_Result_In,
  input  [31:0] M_Result_In,
  input  [31:0] Imm_In,
  output WB_Out,
  output [4:0] RD_Sel_Out,
  output [31:0] Result
);

  Multiplexer #(.select(2), .width(32)) multiplexer_1 (
    .in0(Next_PC_In), .in1(A_Result_In), .in2(M_Result_In), .in3(Imm_In), .out(Result), .sel(WB_Sel_In));

  assign RD_Sel_Out = RD_Sel_In;
  assign WB_Out = WB_In;

  // Other names for the same wires on the sheet: A_Result[31:0] = A_Result_In; Imm[31:0] = Imm_In;
  //   M_Result[31:0] = M_Result_In; Next_PC[31:0] = Next_PC_In; PC[31:0] = PC_In; RD_Sel[4:0] = RD_Sel_In; WB = WB_In;
  //   WB_Sel[1:0] = WB_Sel_In
endmodule
